# Fritzing sketch boxtop60 (saved by Fritzing 0.9.2b)
circuit board: 8.9982cm x 5.59741cm
breadboards: 1

parts:
  J1 = female pin header, 4 pins [form="♀ (female)"]
  J2 = female pin header, 4 pins [form="♀ (female)"]
  U4R = female pin header, 25 pins [form="♀ (female)"]
  U4L = female pin header, 25 pins [form="♀ (female)"]
  D1 = female pin header, 2 pins [form="♀ (female)"]
  A = RCA [package=rca_lock]
  V = RCA [package=rca_lock]
  5VDC = Power plug
  POWER = Toggle Switch [package=THT]
  D1_2 = LED - 5mm [color="Red (633nm)" package="5 mm [THT]"]
  U5 = TSOP56 [chip_label=IC package=TSOP56]
  ROM = Toggle Switch [package=THT]
  D2 = Rectifier Diode [part_number=1N4001 package="300 mil [THT]"]
  S1 = Toggle Switch [package=THT]
  POLARITY = Toggle Switch [package=THT]
  RESET = Pushbutton [package="[THT]"]

nets:
  N1: J1.pin1, RESET.Pin_1, RESET.Pin_2
  N2: J1.pin2, RESET.Pin_3, RESET.Pin_4
  N3: J1.pin3, POWER.L1
  N4: J1.pin4, POWER.COM
  N5: J2.pin1, A.PIN, A.SWITCH
  N6: J2.pin2, V.PIN, V.SWITCH
  N7: J2.pin3, U4L.pin16, A.SHELL, V.SHELL, U5.16, U5.33, U5.52, ROM.L2, S1.COM
  N8: J2.pin4, D2.cathode
  N9: U4R.pin4, U5.12
  N10: U4R.pin5, U5.11
  N11: U4R.pin6, U5.10
  N12: U4R.pin7, U5.9
  N13: U4R.pin8, U5.8
  N14: U4R.pin9, U5.7
  N15: U4R.pin10, U5.6
  N16: U4R.pin11, U5.5
  N17: U4R.pin12, U5.4
  N18: U4R.pin13, U5.3
  N19: U4R.pin14, U5.54
  N20: U4R.pin15, U5.2
  N21: U4R.pin16, U5.1
  N22: U4R.pin17, U5.51
  N23: U4R.pin18, U5.50
  N24: U4R.pin19, U5.49
  N25: U4R.pin20, U5.48
  N26: U4R.pin21, U5.47
  N27: U4R.pin22, U5.46
  N28: U4R.pin23, U5.45
  N29: U4R.pin24, U5.44
  N30: U4R.pin25, U5.13, U5.14, U5.29, U5.43, ROM.L1
  N31: U4L.pin3, U5.56
  N32: U4L.pin4, U5.15
  N33: U4L.pin5, U5.18
  N34: U4L.pin6, U5.19
  N35: U4L.pin7, U5.20
  N36: U4L.pin8, U5.21
  N37: U4L.pin9, U5.22
  N38: U4L.pin10, U5.23
  N39: U4L.pin11, U5.24
  N40: U4L.pin12, U5.25
  N41: U4L.pin13, U5.26
  N42: U4L.pin14, U5.31
  N43: U4L.pin15, U5.32
  N44: U4L.pin17, U5.34
  N45: U4L.pin18, U5.35
  N46: U4L.pin19, U5.36
  N47: U4L.pin20, U5.37
  N48: U4L.pin21, U5.38
  N49: U4L.pin22, U5.39
  N50: U4L.pin23, U5.40
  N51: U4L.pin24, U5.41
  N52: U4L.pin25, U5.42
  N53: D1.pin1, D1_2.anode
  N54: D1.pin2, D1_2.cathode
  N55: 5VDC.GND, S1.L1, POLARITY.L2
  N56: 5VDC.VCC, S1.L2, POLARITY.L1
  N57: U5.55, ROM.COM
  N58: D2.anode, POLARITY.COM
