# Fritzing sketch jamma-led-joystick (saved by Fritzing 0.9.2b)
circuit board: 7.67853cm x 4.26307cm
breadboards: 1

parts:
  J8 = molex pin header, 2 pins [form=molex]
  J9 = molex pin header, 2 pins [form=molex]
  J10 = molex pin header, 2 pins [form=molex]
  J11 = molex pin header, 2 pins [form=molex]
  J12 = molex pin header, 2 pins [form=molex]
  J13 = molex pin header, 5 pins [form=molex]
  J26 = molex pin header, 3 pins [form=molex]
  J27 = molex pin header, 3 pins [form=molex]
  J28 = molex pin header, 3 pins [form=molex]
  J29 = molex pin header, 3 pins [form=molex]
  J30 = molex pin header, 3 pins [form=molex]
  J31 = molex pin header, 3 pins [form=molex]
  J32 = molex pin header, 3 pins [form=molex]
  J33 = molex pin header, 3 pins [form=molex]
  J34 = molex pin header, 3 pins [form=molex]
  J35 = molex pin header, 3 pins [form=molex]
  J36 = molex pin header, 3 pins [form=molex]
  J37 = molex pin header, 3 pins [form=molex]
  J38 = molex pin header, 2 pins [form=molex]
  J39 = Screw terminal - 2 pins [package=THT]
  J43 = female pin header, 8 pins [form="♀ (female)"]
  J44 = female pin header, 8 pins [form="♀ (female)"]
  J42 = female pin header, 6 pins [form="♀ (female)"]

nets:
  N1: J8.pin1, J13.pin1, J42.pin2
  N2: J8.pin2, J9.pin2, J10.pin2, J11.pin2, J12.pin2, J13.pin5, J26.pin1, J27.pin1, J28.pin1, J29.pin1, J30.pin1, J31.pin1, J32.pin1, J33.pin1, J34.pin1, J35.pin1, J36.pin1, J37.pin1, J38.pin2, J39.pin2, J43.pin1, J44.pin1, J42.pin1
  N3: J9.pin1, J13.pin2, J42.pin3
  N4: J10.pin1, J13.pin3, J42.pin4
  N5: J11.pin1, J13.pin4, J42.pin5
  N6: J12.pin1, J26.pin3, J27.pin3, J28.pin3, J29.pin3, J30.pin3, J31.pin3, J32.pin3, J33.pin3, J34.pin3, J35.pin3, J36.pin3, J37.pin3, J38.pin1, J39.pin1, J43.pin8, J44.pin8, J42.pin6
  N7: J26.pin2, J43.pin2
  N8: J27.pin2, J44.pin2
  N9: J28.pin2, J43.pin3
  N10: J29.pin2, J44.pin3
  N11: J30.pin2, J43.pin4
  N12: J31.pin2, J44.pin4
  N13: J32.pin2, J44.pin5
  N14: J33.pin2, J43.pin5
  N15: J34.pin2, J44.pin6
  N16: J35.pin2, J43.pin6
  N17: J36.pin2, J44.pin7
  N18: J37.pin2, J43.pin7

notes:
  GND
  VCC
  AR
  AD
  AU
  AL
  K1
  K2
  K3
  K4
  K5
  K6
  K7
  K8
  K9
  K10
  K11
  K12
  JAMMA
  led-joystick
