# Fritzing sketch jk03 (saved by Fritzing 0.9.2b)
circuit board: 3.8cm x 1.9cm
breadboards: 1

parts:
  20 = male pin header, 1 pin [form="♂ (male)"]  # not connected
  19 = male pin header, 1 pin [form="♂ (male)"]
  18 = male pin header, 1 pin [form="♂ (male)"]
  16 = male pin header, 1 pin [form="♂ (male)"]
  0 = male pin header, 1 pin [form="♂ (male)"]  # not connected
  1 = male pin header, 1 pin [form="♂ (male)"]
  2 = male pin header, 1 pin [form="♂ (male)"]
  3 = male pin header, 1 pin [form="♂ (male)"]
  4 = male pin header, 1 pin [form="♂ (male)"]
  5 = male pin header, 1 pin [form="♂ (male)"]
  6 = male pin header, 1 pin [form="♂ (male)"]
  7 = male pin header, 1 pin [form="♂ (male)"]
  8 = male pin header, 1 pin [form="♂ (male)"]
  9 = male pin header, 1 pin [form="♂ (male)"]
  10 = male pin header, 1 pin [form="♂ (male)"]
  11 = male pin header, 1 pin [form="♂ (male)"]
  12 = male pin header, 1 pin [form="♂ (male)"]
  13 = male pin header, 1 pin [form="♂ (male)"]
  14 = male pin header, 1 pin [form="♂ (male)"]
  15 = male pin header, 1 pin [form="♂ (male)"]
  17 = male pin header, 1 pin [form="♂ (male)"]
  74LS224 = SSOP20 [chip_label=IC package=SSOP]
  C1 = Ceramic Capacitor [capacitance=100nF package="0805 [SMD, multilayer]"]
  C2 = Ceramic Capacitor [capacitance=100nF package="0805 [SMD, multilayer]"]
  C3 = Ceramic Capacitor [capacitance=100nF package="0805 [SMD, multilayer]"]
  C4 = Ceramic Capacitor [capacitance=100nF package="0805 [SMD, multilayer]"]
  C5 = Ceramic Capacitor [capacitance=100nF package="0805 [SMD, multilayer]"]
  C6 = Ceramic Capacitor [capacitance=100nF package="0805 [SMD, multilayer]"]
  C7 = Ceramic Capacitor [capacitance=100nF package="0805 [SMD, multilayer]"]
  C8 = Ceramic Capacitor [capacitance=100nF package="0805 [SMD, multilayer]"]
  C9 = Ceramic Capacitor [capacitance=100nF package="0805 [SMD, multilayer]"]
  R1 = Resistor [tolerance=±5% resistance=1k package="0805 [SMD]"]
  R2 = Resistor [tolerance=±5% resistance=1k package="0805 [SMD]"]
  R3 = Resistor [tolerance=±5% resistance=1k package="0805 [SMD]"]
  R4 = Resistor [tolerance=±5% resistance=1k package="0805 [SMD]"]
  R5 = Resistor [tolerance=±5% resistance=1k package="0805 [SMD]"]
  R6 = Resistor [tolerance=±5% resistance=1k package="0805 [SMD]"]
  R7 = Resistor [tolerance=±5% resistance=1k package="0805 [SMD]"]
  R8 = Resistor [tolerance=±5% resistance=1k package="0805 [SMD]"]
  R9 = Resistor [tolerance=±5% resistance=47 package="0805 [SMD]"]
  R10 = Resistor [tolerance=±5% resistance=47 package="0805 [SMD]"]
  R11 = Resistor [tolerance=±5% resistance=47 package="0805 [SMD]"]
  R12 = Resistor [tolerance=±5% resistance=47 package="0805 [SMD]"]
  R13 = Resistor [tolerance=±5% resistance=47 package="0805 [SMD]"]
  R14 = Resistor [tolerance=±5% resistance=47 package="0805 [SMD]"]
  R15 = Resistor [tolerance=±5% resistance=47 package="0805 [SMD]"]
  R16 = Resistor [tolerance=±5% resistance=47 package="0805 [SMD]"]

nets:
  N1: 19.pin1, R1.Pin_0, R9.Pin_1
  N2: 18.pin1, 74LS224.3
  N3: 16.pin1, 74LS224.5
  N4: 1.pin1, 74LS224.20, C9.1, R1.Pin_1, R2.Pin_1, R3.Pin_1, R4.Pin_1, R5.Pin_1, R6.Pin_1, R7.Pin_1, R8.Pin_1
  N5: 2.pin1, 74LS224.1, 74LS224.19
  N6: 3.pin1, 74LS224.18
  N7: 4.pin1, R8.Pin_0, R16.Pin_1
  N8: 5.pin1, 74LS224.16
  N9: 6.pin1, R7.Pin_0, R15.Pin_1
  N10: 7.pin1, 74LS224.14
  N11: 8.pin1, R6.Pin_0, R14.Pin_1
  N12: 9.pin1, 74LS224.12
  N13: 10.pin1, R5.Pin_0, R13.Pin_1
  N14: 11.pin1, 74LS224.10, C1.0, C2.0, C3.0, C4.0, C5.0, C6.0, C7.0, C8.0, C9.0
  N15: 12.pin1, 74LS224.9
  N16: 13.pin1, R4.Pin_0, R12.Pin_1
  N17: 14.pin1, 74LS224.7
  N18: 15.pin1, R3.Pin_0, R11.Pin_1
  N19: 17.pin1, R2.Pin_0, R10.Pin_1
  N20: 74LS224.2, C1.1, R9.Pin_0
  N21: 74LS224.4, C2.1, R10.Pin_0
  N22: 74LS224.6, C3.1, R11.Pin_0
  N23: 74LS224.8, C4.1, R12.Pin_0
  N24: 74LS224.11, C5.1, R13.Pin_0
  N25: 74LS224.13, C6.1, R14.Pin_0
  N26: 74LS224.15, C7.1, R15.Pin_0
  N27: 74LS224.17, C8.1, R16.Pin_0

notes:
  1
  19
  Jaleco JK-03 Replica
  18
  17
  16
  15
  14
  13
  12
  11
  10
  2
  3
  4
  5
  6
  7
  8
  9
  JK-03
  Replica
  Jaleco
