# Fritzing sketch syncstripper (saved by Fritzing 0.9.2b)
circuit board: 3.2cm x 2cm
breadboards: 1

parts:
  LM1881N = IC, DIP package, 8 pins [chip_label=IC]
  R1 = Resistor [tolerance=±5% resistance=680k package=THT]
  R2 = Resistor [tolerance=±5% resistance=680 package=THT]
  C1 = Ceramic Capacitor [capacitance=100nF package="100 mil [THT, multilayer]"]
  C2 = Ceramic Capacitor [capacitance=100nF package="100 mil [THT, multilayer]"]
  S1 = Toggle Switch [package=THT]
  J1 = molex pin header, 2 pins [form=molex]
  J2 = Screw terminal - 2 pins [package=THT]
  J3 = Screw terminal - 2 pins [package=THT]

nets:
  N1: LM1881N.pin1, R2.Pin_1
  N2: LM1881N.pin2, C2.1
  N3: LM1881N.pin4, R1.Pin_1, C1.1, J1.pin1, J3.pin1
  N4: LM1881N.pin6, R1.Pin_0, C1.0
  N5: LM1881N.pin8, J1.pin2, J3.pin2
  N6: R2.Pin_0, S1.L1
  N7: C2.0, S1.L2, J2.pin1
  N8: S1.COM, J2.pin2

notes:
  IN
  OUT
  ON
  OFF
  GND
  VCC
  SyncStripper
